# Fritzing sketch schematic (saved by Fritzing 0.9.2b)
breadboards: 1

parts:
  U1 = PIC16F874A/877A [package=dil40]
  S1 = Momentary Switch [package=ksa_sealed_tac_switch]
  S2 = Round Pushbutton
  S3 = Momentary Switch [package=ksa_sealed_tac_switch]
  R1 = Resistor [tolerance=±5% resistance=22 package="2010 [SMD]"]
  T1 = LM35 Temperature Sensor [package="TO92 [THT]"]
  Q1 = MOSFET-NCHANNEL [package=to-92]
  V1 = DC Power [voltage=5V]
  V2 = DC Power [voltage=12V]
  FAN = DC Motor
  7SEG1 = LCD I2C (green)
  V1_2 = DC Power [voltage=5V]

nets:
  N1: U1.RA0/AN0, T1.Vout
  N2: U1.RE0/RD/AN5, Q1.G
  N3: U1.RC3/SCK/SCL, 7SEG1.SCL
  N4: U1.RD3/PSP3, S2.leg1
  N5: U1.RC4/SDI/SDA, 7SEG1.SDA
  N6: U1.RD4/PSP4, S3.4
  N7: U1.RD5/PSP5, S1.4
  VSS: U1.VSS, T1.GND, V1.V-
  N8: U1.VDD, S1.1, S2.leg0, S3.1, T1.+Vs, V1.V+
  N9: R1.Pin_0, V2.V-, FAN.pin_2
  N10: R1.Pin_1, Q1.D
  N11: Q1.S, V2.V+, FAN.pin_1
  N12: 7SEG1.V+, V1_2.V+
  N13: 7SEG1.GND, V1_2.V-

custom parts:
  PIC16F874A/877A: Microchip 6-bit
  LCD I2C (green): 4-digit, 7-segment LED Display with I2C Control
